// Logisim project MuxDemux.circ as structural Verilog: 2 circuits, main circuit main
module main (
  input  d0,
  input  d1,
  input  d2,
  input  d0_2,
  input  d3,
  input  d1_2,
  input  in_7,
  input  in_8,
  input  in_9,
  input  s,
  input  d7,
  input  [2:0] s0__s1__s2,
  input  d0_3,
  input  d1_3,
  input  d0_4,
  input  d2_2,
  input  d1_4,
  input  d2_3,
  input  d3_2,
  input  d3_3,
  input  [1:0] s0_and_s1,
  input  d4,
  input  in_23,
  input  in_24,
  input  in_25,
  input  d8,
  input  in_27,
  input  in_28,
  input  in_29,
  input  in_30,
  input  in_31,
  input  in_32,
  input  d15,
  input  [3:0] s0__s1__s2__s3,
  output Y,
  output Y_2,
  output Y_3,
  output Y_4
);

  Multiplexer #(.enable("false")) multiplexer_1 (.in0(d0_2), .in1(d1_2), .out(Y_2), .sel(s));
  Multiplexer #(.select(2), .enable("false")) multiplexer_2 (
    .in0(d0_3), .in1(d1_3), .in2(d2_2), .in3(d3_2), .out(Y_3), .sel(s0_and_s1));
  Multiplexer #(.select(3), .enable("false")) multiplexer_3 (
    .in0(d0), .in1(d1), .in2(d2), .in3(d3), .in4(in_7), .in5(in_8), .in6(in_9), .in7(d7), .out(Y),
    .sel(s0__s1__s2));
  Multiplexer #(.select(4), .enable("false")) multiplexer_4 (
    .in0(d0_4), .in1(d1_4), .in2(d2_3), .in3(d3_3), .in4(d4), .in5(in_23), .in6(in_24), .in7(in_25),
    .in8(d8), .in9(in_27), .in10(in_27), .in11(in_29), .in12(in_30), .in13(in_31), .in14(in_32), .in15(d15),
    .out(Y_4), .sel(s0__s1__s2__s3));

  assign in_28 = in_27;

  // Notes on the sheet:
  //   2to1 Multiplexer
  //   4to1 Multiplexer
  //   16to1 Multiplexer
  //   8to1 Multiplexer
endmodule

module demucs (
  input  y,
  input  s0,
  input  y_2,
  input  [1:0] s0_and_s1,
  input  y_3,
  input  [2:0] s0_s1_and_s2,
  input  y_4,
  input  [3:0] s0_s1_s2_and_s3,
  output d0,
  output d1,
  output d0_2,
  output d1_2,
  output d2,
  output d3,
  output d0_3,
  output d1_3,
  output d2_2,
  output d3_2,
  output d4,
  output d5,
  output d6,
  output d7,
  output d0_4,
  output d1_4,
  output d2_3,
  output d3_3,
  output d4_2,
  output d5_2,
  output out_29,
  output out_30,
  output out_31,
  output out_32,
  output out_33,
  output out_34,
  output d12,
  output d13,
  output d14,
  output d15
);

  Demultiplexer #(.enable("false")) demultiplexer_1 (.out0(d0), .out1(d1), .in(y), .sel(s0));
  Demultiplexer #(.select(2), .enable("false")) demultiplexer_2 (
    .out0(d0_2), .out1(d1_2), .out2(d2), .out3(d3), .in(y_2), .sel(s0_and_s1));
  Demultiplexer #(.select(3), .enable("false")) demultiplexer_3 (
    .out0(d0_3), .out1(d1_3), .out2(d2_2), .out3(d3_2), .out4(d4), .out5(d5), .out6(d6), .out7(d7), .in(y_3),
    .sel(s0_s1_and_s2));
  Demultiplexer #(.select(4), .enable("false")) demultiplexer_4 (
    .out0(d0_4), .out1(d1_4), .out2(d2_3), .out3(d3_3), .out4(d4_2), .out5(d5_2), .out6(out_29),
    .out7(out_30), .out8(out_31), .out9(out_32), .out10(out_33), .out11(out_34), .out12(d12), .out13(d13),
    .out14(d14), .out15(d15), .in(y_4), .sel(s0_s1_s2_and_s3));

  // Notes on the sheet:
  //   1to8 DeMultiplexer
  //   1to2 DeMultiplexer
  //   1to16 DeMultiplexer
  //   1to4 DeMultiplexer
endmodule
